# Fritzing sketch light_control_circuit (saved by Fritzing 0.9.0b)
breadboards: 1

parts:
  Part1 = Arduino Uno (Rev3)
  PIR1 = PIR sensor
  PIR2 = PIR sensor
  LED1 = Super Flux LED blue [color=Blue]
  R1 = Resistor [tolerance=±5% resistance=220 package=THT]
  R2 = PHOTOCELL [package=photocell]
  R3 = Resistor [tolerance=±5% resistance=220 package=THT]
  U1 = RELAY [package=relay-t9a-2]
  U2 = RELAY [package=relay-t9a-2]
  LED2 = LED - 5mm [color="Red (633nm)" package="5 mm [THT]"]  # not connected
  R4 = Resistor [tolerance=±5% resistance=220 package=THT]
  LED3 = Super Flux LED blue [color=Blue]
  R5 = Resistor [tolerance=±5% resistance=220 package=THT]

nets:
  N1: Part1.A0, R2.P$1, R3.Pin_1
  N2: Part1.D8, PIR2.SIG
  N3: Part1.D9_PWM, U2.MAIN
  N4: Part1.D11_PWM/MOSI, R5.Pin_1
  N5: Part1.D3_PWM, LED1.anode
  N6: Part1.D5_PWM, U1.MAIN
  N7: Part1.D7, PIR1.SIG
  VDD: Part1.5V, PIR1.VDD, PIR2.VDD, R3.Pin_0, U1.COIL2, U2.COIL2, LED3.cathode
  GND: Part1.GND, PIR1.GND, PIR2.GND, R1.Pin_1, R2.P$2, U1.COIL1, U2.COIL1, R4.Pin_1
  N8: LED1.cathode, R1.Pin_0
  N9: LED3.anode, R5.Pin_0

notes:
  PIR for main light, connect to pin 7
  PIR for bath_room light, connect to pin 8
  blue Led while mail light PIR high,connect to pin 3
  photocell for main room, connect to A0
  bath light relay
  light detect switch connect to pin 4
  PIR detect switch for main light
