# Fritzing sketch light_control_circuit (saved by Fritzing 0.9.0b)
breadboards: 1

parts:
  Part1 = Arduino Uno (Rev3)
  PIR1 = PIR sensor
  R1 = Resistor [tolerance=±5% resistance=220 package=THT]
  R2 = Photocell (LDR) [package=THT]
  LED2 = Super Flux LED blue [color=Blue]
  LED3 = LED - 5mm [color="Red (633nm)" package="5 mm [THT]"]
  R3 = Resistor [tolerance=±5% resistance=220 package=THT]
  U1 = RELAY [package=relay-t9a-2]
  J1 = Basic Servo
  PIR2 = PIR sensor
  LED4 = LED - 5mm [color="Red (633nm)" package="5 mm [THT]"]
  R4 = Resistor [tolerance=±5% resistance=220 package=THT]
  LED5 = LED - 5mm [color="Red (633nm)" package="5 mm [THT]"]
  R5 = Resistor [tolerance=±5% resistance=220 package=THT]
  U2 = RELAY [package=relay-t9a-2]
  LED6 = LED - 5mm [color="Red (633nm)" package="5 mm [THT]"]
  R6 = Resistor [tolerance=±5% resistance=220 package=THT]

nets:
  GND: Part1.A0, Part1.GND, PIR1.GND, R1.Pin_1, R2.pin_1, LED2.anode, R3.Pin_1, U1.COIL1, J1.gnd, PIR2.GND, R4.Pin_1, R5.Pin_1, U2.COIL1
  N1: Part1.D3_PWM, PIR1.SIG, LED3.cathode
  N2: Part1.D4, U1.MAIN, LED5.anode
  N3: Part1.D5_PWM, J1.pulse
  N4: Part1.D6_PWM, PIR2.SIG, LED4.cathode
  N5: Part1.D7, U2.MAIN, LED6.anode
  VDD: PIR1.VDD, R2.pin_0, U1.COIL2, J1.vcc, PIR2.VDD, U2.COIL2
  N6: R1.Pin_0, LED3.anode
  N7: LED2.cathode, R3.Pin_0
  N8: LED4.anode, R4.Pin_0
  N9: LED5.cathode, R5.Pin_0
  N10: LED6.cathode, R6.Pin_0

notes:
  main light PIR, 3
  light photocell for main room
